# Fritzing sketch Breadborad-Werkstatt (saved by Fritzing 0.9.3b)
perfboards: 1
stripboards: 1

parts:
  J2 = double row female pin header, 4 pins [form="♀ (female)"]
  J3 = double row female pin header, 4 pins [form="♀ (female)"]
  J1 = double row female pin header, 6 pins [form="♀ (female)"]
  RHT1 = Humidity and Temperature Sensor RHT03
  S1 = Pushbutton [package=THT]
  J4 = double row female pin header, 2 pins [form="♀ (female)"]
  J6 = double row female pin header, 4 pins [form="♀ (female)"]
  J5 = double row female pin header, 2 pins [form="♀ (female)"]
  J7 = double row female pin header, 4 pins [form="♀ (female)"]
  J8 = double row female pin header, 4 pins [form="♀ (female)"]
  J9 = double row female pin header, 6 pins [form="♀ (female)"]
  J10 = double row female pin header, 4 pins [form="♀ (female)"]
  RHT2 = Humidity and Temperature Sensor RHT03  # not connected
  J11 = double row female pin header, 2 pins [form="♀ (female)"]
  J12 = double row female pin header, 2 pins [form="♀ (female)"]
  S2 = Pushbutton [package=THT]

nets:
  N1: J2.pin1, J3.pin1, RHT1.Vcc, J5.pin1
  N2: J2.pin4, J1.pin4
  N3: J3.pin2, RHT1.Data-signal, J6.pin3
  N4: J3.pin3, RHT1.GND_2
  N5: J1.pin6, J6.pin4, J5.pin2
  N6: S1.leg0, J4.pin2, J6.pin1
  N7: S1.leg1, J4.pin1
  N8: J7.pin1, J10.pin4, J11.pin2, J12.pin1, S2.leg0
  N9: J7.pin4, J10.pin3
  N10: J8.pin1, J9.pin4
  N11: J8.pin3, J12.pin2, S2.leg1
  N12: J8.pin4, J9.pin6, J10.pin1, J11.pin1

notes:
  3V CH RS TX
  RX 00 02 GND
  HAS POWER (VIA FTDI 3V)
  DOOR OPEN
  GPIO2
  POWER
  DHT22
  GPIO1  (TX)
  GPIO3  (RX)
  GND
  3V
  INNEN
